# Fritzing sketch diagram-with-proto-board (saved by Fritzing 0.9.4)
stripboards: 1

parts:
  Pro_Micro1 = SparkFun Pro Micro
  U1 = POT [package=pot_alpha_rv16af-20]
  SparkFun_74HC4051_8-Channel_Mux_Breakout1 = SparkFun-74HC4051-8-Channel-Mux-Breakout [part_number=BOB-13906]
  R1 = Resistor [tolerance=±5% resistance=1k package="2010 [SMD]"]
  J1 = Piezo Speaker
  U2 = POT [package=pot_alpha_rv16af-20]
  R2 = Resistor [tolerance=±5% resistance=1k package="2010 [SMD]"]
  R3 = Resistor [tolerance=±5% resistance=1k package="2010 [SMD]"]
  R4 = Resistor [tolerance=±5% resistance=1k package="2010 [SMD]"]
  R5 = Resistor [tolerance=±5% resistance=1k package="2010 [SMD]"]
  R6 = Resistor [tolerance=±5% resistance=1k package="2010 [SMD]"]
  R7 = Resistor [tolerance=±5% resistance=1k package="2010 [SMD]"]
  R8 = Resistor [tolerance=±5% resistance=1k package="2010 [SMD]"]
  J2 = Piezo Speaker
  J3 = Piezo Speaker
  J4 = Piezo Speaker
  J5 = Piezo Speaker
  J6 = Piezo Speaker
  J7 = Piezo Speaker
  J8 = Piezo Speaker

nets:
  GND: Pro_Micro1.GND, SparkFun_74HC4051_8-Channel_Mux_Breakout1.GND, R1.Pin_0, R2.Pin_0, R3.Pin_0, R4.Pin_0, R5.Pin_0, R6.Pin_0, R7.Pin_0, R8.Pin_0
  N1: Pro_Micro1.3, Pro_Micro1.4
  N2: Pro_Micro1.A1, U1.S
  N3: Pro_Micro1.A2, U2.S
  N4: Pro_Micro1.VCC, U1.E, U2.E
  N5: U1.A, J1.pin1, U2.A, J2.pin1, J3.pin1, J4.pin1, J5.pin1, J6.pin1, J7.pin1
  N6: R1.Pin_1, J1.pin2
  N7: R2.Pin_1, J2.pin2
  N8: R3.Pin_1, J3.pin2
  N9: R4.Pin_1, J4.pin2
  N10: R5.Pin_1, J5.pin2
  N11: R6.Pin_1, J6.pin2
  N12: R7.Pin_1, J7.pin2
  N13: R8.Pin_1, J8.pin2

custom parts:
  SparkFun Pro Micro: The Pro Micro is similar to the Pro Mini except with an ATmega32U4 on board. The USB transceiver inside the 32U4 allows us to add USB connectivity on-board and do away with bulky external USB interface. Based on: https://github.com/unorthodox-engineers/unorthodox-arduino/blob/master/Unorthodox/fritzing/parts/Pro%20Micro.fzpz
