# Fritzing sketch draft-PCB-design (saved by Fritzing 0.9.4)
circuit board: 8.46667cm x 5.64444cm
stripboards: 1

parts:
  Pro_Micro1 = SparkFun Pro Micro
  U1 = POT [package=pot_alpha_rv16af-20]
  SparkFun_74HC4051_8-Channel_Mux_Breakout1 = SparkFun-74HC4051-8-Channel-Mux-Breakout [part_number=BOB-13906]
  J1 = Piezo Speaker
  U2 = POT [package=pot_alpha_rv16af-20]
  R1 = Resistor [tolerance=±5% resistance=1k package=THT]
  R2 = Resistor [tolerance=±5% resistance=1k package=THT]
  R3 = Resistor [tolerance=±5% resistance=1k package=THT]
  J2 = Piezo Speaker
  J3 = Piezo Speaker
  J4 = Piezo Speaker
  J5 = Piezo Speaker
  J6 = Piezo Speaker
  J7 = Piezo Speaker
  J8 = Piezo Speaker
  R4 = Resistor [tolerance=±5% resistance=1k package=THT]
  R5 = Resistor [tolerance=±5% resistance=1k package=THT]
  R6 = Resistor [tolerance=±5% resistance=1k package=THT]
  R7 = Resistor [tolerance=±5% resistance=1k package=THT]
  R8 = Resistor [tolerance=±5% resistance=1k package=THT]

nets:
  N1: Pro_Micro1.GND, U1.A, J1.pin1, U2.A, R1.Pin_0, R2.Pin_0, R3.Pin_0, J2.pin1, J3.pin1, J4.pin1, J5.pin1, J6.pin1, J7.pin1, J8.pin1, R4.Pin_0, R5.Pin_0, R6.Pin_0, R7.Pin_0, R8.Pin_0
  N2: Pro_Micro1.2, SparkFun_74HC4051_8-Channel_Mux_Breakout1.S2
  N3: Pro_Micro1.3, SparkFun_74HC4051_8-Channel_Mux_Breakout1.S1
  N4: Pro_Micro1.4, SparkFun_74HC4051_8-Channel_Mux_Breakout1.S0
  N5: Pro_Micro1.A0, SparkFun_74HC4051_8-Channel_Mux_Breakout1.Z
  N6: Pro_Micro1.A1, U2.S
  N7: Pro_Micro1.A2, U1.S
  N8: Pro_Micro1.VCC, U1.E, U2.E
  N9: SparkFun_74HC4051_8-Channel_Mux_Breakout1.Y7, J8.pin2, R8.Pin_1
  N10: SparkFun_74HC4051_8-Channel_Mux_Breakout1.Y6, J7.pin2, R7.Pin_1
  N11: SparkFun_74HC4051_8-Channel_Mux_Breakout1.Y5, J6.pin2, R6.Pin_1
  N12: SparkFun_74HC4051_8-Channel_Mux_Breakout1.Y4, J5.pin2, R5.Pin_1
  N13: SparkFun_74HC4051_8-Channel_Mux_Breakout1.Y3, J4.pin2, R4.Pin_1
  N14: SparkFun_74HC4051_8-Channel_Mux_Breakout1.Y2, R3.Pin_1, J3.pin2
  N15: SparkFun_74HC4051_8-Channel_Mux_Breakout1.Y1, R2.Pin_1, J2.pin2
  N16: SparkFun_74HC4051_8-Channel_Mux_Breakout1.Y0, J1.pin2, R1.Pin_1

custom parts:
  SparkFun Pro Micro: The Pro Micro is similar to the Pro Mini except with an ATmega32U4 on board. The USB transceiver inside the 32U4 allows us to add USB connectivity on-board and do away with bulky external USB interface. Based on: https://github.com/unorthodox-engineers/unorthodox-arduino/blob/master/Unorthodox/fritzing/parts/Pro%20Micro.fzpz
